# Fritzing sketch control (saved by Fritzing 0.9.5d)
circuit board: 8.46667cm x 5.64444cm

parts:
  Part1 = Arduino Uno (Rev3)
  TRRS1 = Audio Jack (TRRS) 3.5mm [part_number="LUMBERG JEITA RC-5325A" package="RC-5325A [SMD]"]
  Part2 = InvenSense MPU6050
  Part3 = NRF24L01+ Breakout Board
  U2 = Thumb Joystick [package=joystick]
  Part4 = Arduino Nano (Rev3.0)
  M242-12864-7-V2_0 = WeMos D1 Mini OLED Shield
  Part5 = NRF24L01+ Breakout Board
  Buck_Convertor1 = Buck Convertor [part_number=LM2596 package=THT]
  BAT1 = BC9VPC [package=bc9vpc]

nets:
  N1: Part1.A2, U2.H
  N2: Part1.A3, U2.V
  N3: Part1.A4/SDA, Part2.SDA
  N4: Part1.A5/SCL, Part2.SCL
  N5: Part1.D9_PWM, Part3.CE
  N6: Part1.D10_PWM/SS, Part3.CS
  N7: Part1.D11_PWM/MOSI, Part3.MOSI
  N8: Part1.D12/MISO, Part3.MISO
  N9: Part1.D13/SCK, Part3.SCK
  GND: Part1.GND, Part2.GND, Part3.GND, U2.H-, U2.V-
  3V3: Part1.3V3, Part3.VCC
  5V: Part1.5V, Part2.VCC, U2.V+, U2.H+
  N10: TRRS1.TIP, Buck_Convertor1.Positive_Input, BAT1.V+
  N11: TRRS1.SLEEVE, Buck_Convertor1.Negative_Input, BAT1.V-
  GND_2: Part4.GND, M242-12864-7-V2_0.G, Part5.GND, Buck_Convertor1.Negative_Output
  N12: Part4.D3, M242-12864-7-V2_0.D3
  N13: Part4.D4, M242-12864-7-V2_0.D4
  N14: Part4.D5, M242-12864-7-V2_0.TX
  N15: Part4.D6, M242-12864-7-V2_0.RX
  N16: Part4.D7, M242-12864-7-V2_0.D1
  N17: Part4.D9, Part5.CE
  N18: Part4.D10, Part5.CS
  N19: Part4.D11/MOSI, Part5.MOSI
  N20: Part4.D12/MISO, Part5.MISO
  5V_2: Part4.5V, M242-12864-7-V2_0.5V, Buck_Convertor1.Positive_Output
  3V3_2: Part4.3V3, Part5.VCC
  N21: Part4.D13/SCK, Part5.SCK

custom parts:
  Buck Convertor: DC to DC buck convertor
