# Fritzing sketch drone (saved by Fritzing 0.9.5d)

parts:
  920KV_Motor3 = DJI 920 KV Motor
  920KV_Motor1 = DJI 920 KV Motor
  920KV_Motor2 = DJI 920 KV Motor
  920KV_Motor4 = DJI 920 KV Motor
  M4 = ESC
  M2 = ESC
  M1 = ESC
  M3 = ESC
  Power_plug2 = Power plug  # not connected
  Part1 = Arduino Uno (Rev3)
  Part2 = InvenSense MPU6050
  Part3 = Arduino Nano (Rev3.0)
  Part4 = NRF24L01+ Breakout Board
  Part5 = Arduino Nano (Rev3.0)
  Part6 = NRF24L01+ Breakout Board
  GPS1 = GPS Modul with NEO-6M
  RadiationD1 = Geiger-Counter RadiationD-v1.1 (CAJOE)
  Part7 = Adafruit BME680 [part_number="Adafruit #3660"]

nets (from the breadboard view):
  N1: 920KV_Motor3.w, M3.U
  N2: 920KV_Motor3.v, M3.V
  N3: 920KV_Motor3.u, M3.W
  N4: 920KV_Motor1.w, M1.W
  N5: 920KV_Motor1.v, M1.V
  N6: 920KV_Motor1.u, M1.U
  N7: 920KV_Motor2.w, M2.U
  N8: 920KV_Motor2.v, M2.V
  N9: 920KV_Motor2.u, M2.W
  N10: 920KV_Motor4.w, M4.W
  N11: 920KV_Motor4.v, M4.V
  N12: 920KV_Motor4.u, M4.U
  N13: M4.DATA, Part1.D4
  GND: M4.GND, M2.GND, M1.GND, M3.GND, Part1.GND, Part3.RESET, Part3.GND, Part3.VIN, Part4.GND
  5V: M4.5V, M2.5V, M1.5V, M3.5V, Part1.5V
  N14: M2.DATA, Part1.D5_PWM
  N15: M1.DATA, Part1.D6_PWM
  N16: M3.DATA, Part1.D7
  N17: Part1.A4/SDA, Part2.SDA
  N18: Part1.A5/SCL, Part2.SCL
  N19: Part1.D8, Part3.D2
  N20: Part1.D9_PWM, Part3.D3
  N21: Part1.D10_PWM/SS, Part3.D4
  N22: Part1.D11_PWM/MOSI, Part3.D5
  N23: Part3.D9, Part4.CE
  N24: Part3.D10, Part4.CS
  N25: Part3.D11/MOSI, Part4.MOSI
  N26: Part3.D12/MISO, Part4.MISO
  5V_2: Part3.5V, Part4.VCC
  N27: Part3.D13/SCK, Part4.SCK
  GND_2: Part5.GND, Part6.GND, RadiationD1.GND
  N28: Part5.D2, RadiationD1.INT
  N29: Part5.D3, GPS1.TX
  N30: Part5.D4, GPS1.RX
  N31: Part5.D9, Part6.CE
  N32: Part5.D10, Part6.CS
  N33: Part5.D11/MOSI, Part6.MOSI
  N34: Part5.D12/MISO, Part6.MISO
  5V_3: Part5.5V, RadiationD1.5V
  N35: Part5.A5, Part7.SCK/SCL
  N36: Part5.A4, Part7.SDO/ADR
  3V3: Part5.3V3, Part6.VCC
  N37: Part5.D13/SCK, Part6.SCK

notes:
  ADAPTER

custom parts:
  DJI 920 KV Motor: DJI Brushless Outrunner 2212/920K Motor F330-550
  GPS Modul with NEO-6M: GY-GPS6MV2
  Geiger-Counter RadiationD-v1.1 (CAJOE): with Geiger Müller Tube
